// Logisim project CO-SingleCircleMipsCpu.circ as structural Verilog: 8 circuits, main circuit main
// Registers
module GRF (
  input  clk,
  input  reset,
  input  [4:0] A2,
  input  [4:0] A1,
  input  [31:0] WD,
  input  WE3,
  input  [4:0] A3,
  output [31:0] RD2,
  output [31:0] RD1
);

  wire [31:0] in1, in2, in3, in4, in5, in6, in7, in8, in9, in10, in11, in12, in13, in14, in15, in16, in17,
       in18, in19, in20, in21, in22, in23, in24, in25, in26, in27, in28, in29, in30, in31, None, out1, out2,
       out3, out4, out5, out6, out7, out8, out9, out10, out11, out12, out13, out14, out15, out16, out17,
       out18, out19, out20, out21, out22, out23, out24, out25, out26, out27, out28, out29, out30, out31;

  Register #(.width(32)) register_1 (.D(None), .clk(clk), .clr(reset));  // open: en, Q
  Register #(.width(32)) register_2 (.D(in8), .Q(out8), .clk(clk), .clr(reset));  // open: en
  Register #(.width(32)) register_3 (.D(in16), .Q(out16), .clk(clk), .clr(reset));  // open: en
  Register #(.width(32)) register_4 (.D(in24), .Q(out24), .clk(clk), .clr(reset));  // open: en
  Register #(.width(32)) register_5 (.D(in1), .Q(out1), .clk(clk), .clr(reset));  // open: en
  Register #(.width(32)) register_6 (.D(in9), .Q(out9), .clk(clk), .clr(reset));  // open: en
  Register #(.width(32)) register_7 (.D(in17), .Q(out17), .clk(clk), .clr(reset));  // open: en
  Register #(.width(32)) register_8 (.D(in25), .Q(out25), .clk(clk), .clr(reset));  // open: en
  Demultiplexer #(.select(5), .width(32), .tristate("true")) demultiplexer_1 (
    .out0(None), .out1(in1), .out2(in2), .out3(in3), .out4(in4), .out5(in5), .out6(in6), .out7(in7),
    .out8(in8), .out9(in9), .out10(in10), .out11(in11), .out12(in12), .out13(in13), .out14(in14),
    .out15(in15), .out16(in16), .out17(in17), .out18(in18), .out19(in19), .out20(in20), .out21(in21),
    .out22(in22), .out23(in23), .out24(in24), .out25(in25), .out26(in26), .out27(in27), .out28(in28),
    .out29(in29), .out30(in30), .out31(in31), .in(WD), .sel(A3), .en(WE3));
  Register #(.width(32)) register_9 (.D(in2), .Q(out2), .clk(clk), .clr(reset));  // open: en
  Register #(.width(32)) register_10 (.D(in10), .Q(out10), .clk(clk), .clr(reset));  // open: en
  Register #(.width(32)) register_11 (.D(in18), .Q(out18), .clk(clk), .clr(reset));  // open: en
  Register #(.width(32)) register_12 (.D(in26), .Q(out26), .clk(clk), .clr(reset));  // open: en
  Multiplexer #(.select(5), .width(32), .disabled(0)) multiplexer_1 (
    .in0({32{1'b0}}), .in1(out1), .in2(out2), .in3(out3), .in4(out4), .in5(out5), .in6(out6), .in7(out7),
    .in8(out8), .in9(out9), .in10(out10), .in11(out11), .in12(out12), .in13(out13), .in14(out14),
    .in15(out15), .in16(out16), .in17(out17), .in18(out18), .in19(out19), .in20(out20), .in21(out21),
    .in22(out22), .in23(out23), .in24(out24), .in25(out25), .in26(out26), .in27(out27), .in28(out28),
    .in29(out29), .in30(out30), .in31(out31), .out(RD1), .sel(A1));  // open: en
  Register #(.width(32)) register_13 (.D(in3), .Q(out3), .clk(clk), .clr(reset));  // open: en
  Register #(.width(32)) register_14 (.D(in11), .Q(out11), .clk(clk), .clr(reset));  // open: en
  Register #(.width(32)) register_15 (.D(in19), .Q(out19), .clk(clk), .clr(reset));  // open: en
  Register #(.width(32)) register_16 (.D(in27), .Q(out27), .clk(clk), .clr(reset));  // open: en
  Register #(.width(32)) register_17 (.D(in4), .Q(out4), .clk(clk), .clr(reset));  // open: en
  Register #(.width(32)) register_18 (.D(in12), .Q(out12), .clk(clk), .clr(reset));  // open: en
  Register #(.width(32)) register_19 (.D(in20), .Q(out20), .clk(clk), .clr(reset));  // open: en
  Register #(.width(32)) register_20 (.D(in28), .Q(out28), .clk(clk), .clr(reset));  // open: en
  Register #(.width(32)) register_21 (.D(in5), .Q(out5), .clk(clk), .clr(reset));  // open: en
  Register #(.width(32)) register_22 (.D(in13), .Q(out13), .clk(clk), .clr(reset));  // open: en
  Register #(.width(32)) register_23 (.D(in21), .Q(out21), .clk(clk), .clr(reset));  // open: en
  Register #(.width(32)) register_24 (.D(in29), .Q(out29), .clk(clk), .clr(reset));  // open: en
  Register #(.width(32)) register_25 (.D(in6), .Q(out6), .clk(clk), .clr(reset));  // open: en
  Register #(.width(32)) register_26 (.D(in14), .Q(out14), .clk(clk), .clr(reset));  // open: en
  Register #(.width(32)) register_27 (.D(in22), .Q(out22), .clk(clk), .clr(reset));  // open: en
  Register #(.width(32)) register_28 (.D(in30), .Q(out30), .clk(clk), .clr(reset));  // open: en
  Register #(.width(32)) register_29 (.D(in7), .Q(out7), .clk(clk), .clr(reset));  // open: en
  Register #(.width(32)) register_30 (.D(in15), .Q(out15), .clk(clk), .clr(reset));  // open: en
  Register #(.width(32)) register_31 (.D(in23), .Q(out23), .clk(clk), .clr(reset));  // open: en
  Register #(.width(32)) register_32 (.D(in31), .Q(out31), .clk(clk), .clr(reset));  // open: en
  Multiplexer #(.select(5), .width(32), .disabled(0)) multiplexer_2 (
    .in0({32{1'b0}}), .in1(out1), .in2(out2), .in3(out3), .in4(out4), .in5(out5), .in6(out6), .in7(out7),
    .in8(out8), .in9(out9), .in10(out10), .in11(out11), .in12(out12), .in13(out13), .in14(out14),
    .in15(out15), .in16(out16), .in17(out17), .in18(out18), .in19(out19), .in20(out20), .in21(out21),
    .in22(out22), .in23(out23), .in24(out24), .in25(out25), .in26(out26), .in27(out27), .in28(out28),
    .in29(out29), .in30(out30), .in31(out31), .out(RD2), .sel(A2));  // open: en
endmodule

module main (
  input  Reset,
  output [31:0] out_2,
  output out_3,
  output [4:0] out_4,
  output [31:0] out_5,
  output out_6,
  output [4:0] out_7,
  output [31:0] out_8
);

  wire ALUSrc, Branch, Byte, CLK, J_Control, Jr_Control, MemtoReg, RegDst, ZeroSignal;
  wire [2:0] ALUControl;
  wire [31:0] alu_1_aluresult, bit_extender_1_out, dm_1_rd, multiplexer_2_out, npc_1_npc, PC_value, PCBranch,
       PCPlus4, Register_Read_A, shifter_1_out;

  Register #(.width(32)) PC_Reg (.D(npc_1_npc), .Q(PC_value), .clk(CLK), .clr(Reset));  // open: en
  NPC npc_1 (
    .in_1(PC_value), .in_2(out_2), .in_3(PCBranch), .in_4(Register_Read_A), .in_5(J_Control),
    .in_6(Jr_Control), .in_7(Branch), .in_8(ZeroSignal), .NPC(npc_1_npc));
  Adder #(.width(32)) adder_1 (.a(32'h4), .b(PC_value), .out(PCPlus4));  // open: cin, cout
  IM im_1 (.A(PC_value), .Instr(out_2));
  Control_Unit control_unit_1 (
    .HIGH6(out_2[31:26]), .LOW6(out_2[5:0]), .MemtoReg(MemtoReg), .MemWrite(out_6), .ALUSrc(ALUSrc),
    .Branch(Branch), .RegDst(RegDst), .RegWrite(out_3), .ALUControl(ALUControl), .jump(J_Control),
    .jr(Jr_Control), .Byte_Op(Byte));
  Multiplexer #(.width(5)) multiplexer_1 (
    .in0(out_2[20:16]), .in1(out_2[15:11]), .out(out_4), .sel(RegDst));  // open: en
  Clock u_CLK (.out(CLK));
  GRF grf_1 (
    .reset(Reset), .A3(out_4), .WD(out_5), .WE3(out_3), .RD2(out_8), .RD1(Register_Read_A),
    .A1(out_2[25:21]), .A2(out_2[20:16]), .clk(CLK));
  assign bit_extender_1_out = {{16{out_2[15]}}, out_2[15:0]};  // Bit_Extender bit_extender_1
  Multiplexer #(.width(32)) multiplexer_2 (
    .in0(out_8), .in1(bit_extender_1_out), .out(multiplexer_2_out), .sel(ALUSrc));  // open: en
  Shifter #(.width(32)) shifter_1 (.in(bit_extender_1_out), .\dist (5'b00010), .out(shifter_1_out));
  ALU alu_1 (
    .ALUControl(ALUControl), .SrcA(Register_Read_A), .SrcB(multiplexer_2_out), .Zero(ZeroSignal),
    .ALUResult({alu_1_aluresult[31:7], out_7, alu_1_aluresult[1:0]}));
  Adder #(.width(32)) adder_2 (.a(PCPlus4), .b(shifter_1_out), .out(PCBranch));  // open: cin, cout
  DM dm_1 (
    .A({alu_1_aluresult[31:7], out_7, alu_1_aluresult[1:0]}), .WD(out_8), .RD(dm_1_rd), .WE(out_6),
    .Clk(CLK), .Reset(Reset), .Byte_Op(Byte));
  Multiplexer #(.width(32)) multiplexer_3 (
    .in0({alu_1_aluresult[31:7], out_7, alu_1_aluresult[1:0]}), .in1(dm_1_rd), .out(out_5), .sel(MemtoReg));  // open: en

  // Other names for the same wires on the sheet: MemAddr[4:0] = out_7; Instr[31:0] = out_2; MemData[31:0] = out_8;
  //   MemWrite = out_6; RegAddr[4:0] = out_4; RegWrite = out_3; WriteBack[31:0] = out_5
endmodule

module IM (
  input  [31:0] A,
  output [31:0] Instr
);

  ROM #(.addrWidth(10), .dataWidth(32)) rom_1 (.addr(A[11:2]), .data(Instr));  // open: sel

  // Notes on the sheet:
  //   contents of rom_1 (hex, n*v repeats v):
  //   363100ff 36520004 369403ff ae510000 82540000 a2540002 8000c00
endmodule

module DM (
  input  Byte_Op,
  input  [31:0] A,
  input  WE,
  input  Clk,
  input  Reset,
  input  [31:0] WD,
  output [31:0] RD
);

  wire decoder_1_out0, decoder_1_out1, decoder_1_out2, decoder_1_out3;
  wire [7:0] multiplexer_7_out;
  wire [31:0] LB, multiplexer_1_out, ReadData, SB;

  Multiplexer #(.width(32)) multiplexer_1 (.in0(WD), .in1(SB), .out(multiplexer_1_out), .sel(Byte_Op));  // open: en
  RAM #(.addrWidth(5), .dataWidth(32), .bus("separate")) ram_1 (
    .addr(A[6:2]), .din(multiplexer_1_out), .data(ReadData), .str(WE), .clk(Clk), .clr(Reset));  // open: sel, ld
  Decoder #(.select(2)) decoder_1 (
    .out0(decoder_1_out0), .out1(decoder_1_out1), .out2(decoder_1_out2), .out3(decoder_1_out3), .sel(A[1:0]));  // open: en
  Multiplexer #(.width(32)) multiplexer_2 (.in0(ReadData), .in1(LB), .out(RD), .sel(Byte_Op));  // open: en
  Multiplexer #(.width(8)) multiplexer_3 (
    .in0(ReadData[7:0]), .in1(WD[7:0]), .out(SB[7:0]), .sel(decoder_1_out0));  // open: en
  Multiplexer #(.width(8)) multiplexer_4 (
    .in0(ReadData[15:8]), .in1(WD[7:0]), .out(SB[15:8]), .sel(decoder_1_out1));  // open: en
  Multiplexer #(.width(8)) multiplexer_5 (
    .in0(ReadData[23:16]), .in1(WD[7:0]), .out(SB[23:16]), .sel(decoder_1_out2));  // open: en
  Multiplexer #(.width(8)) multiplexer_6 (
    .in0(ReadData[31:24]), .in1(WD[7:0]), .out(SB[31:24]), .sel(decoder_1_out3));  // open: en
  Multiplexer #(.select(2), .width(8)) multiplexer_7 (
    .in0(ReadData[7:0]), .in1(ReadData[15:8]), .in2(ReadData[23:16]), .in3(ReadData[31:24]),
    .out(multiplexer_7_out), .sel(A[1:0]));  // open: en
  assign LB = {{24{multiplexer_7_out[7]}}, multiplexer_7_out};  // Bit_Extender bit_extender_1

  // Other names for the same wires on the sheet: Byte_Sel[1:0] = A[1:0]; WriteData[31:0] = WD
endmodule

module ALU (
  input  [2:0] ALUControl,
  input  [31:0] SrcA,
  input  [31:0] SrcB,
  output Zero,
  output [31:0] ALUResult
);

  wire [31:0] add, lui, \or , sub;

  Adder #(.width(32)) adder_1 (.a(SrcA), .b(SrcB), .out(add));  // open: cin, cout
  Subtractor #(.width(32)) subtractor_1 (.a(SrcA), .b(SrcB), .out(sub));  // open: bin, bout
  _32bit_or u_32bit_or_1 (.in_1(SrcA), .in_2(SrcB), .out_3(\or ));
  Shifter #(.width(32)) shifter_1 (.in(SrcB), .\dist (5'b10000), .out(lui));
  Multiplexer #(.select(3), .width(32), .disabled(0)) multiplexer_1 (
    .in0(add), .in1(sub), .in2(\or ), .in3(lui), .out(ALUResult), .sel(ALUControl));  // open: in4, in5, in6, in7, en
  Comparator #(.width(32), .mode("unsigned")) comparator_1 (.a({32{1'b0}}), .b(ALUResult), .eq(Zero));  // open: gt, lt

  // Other names for the same wires on the sheet: A[31:0] = SrcA; B[31:0] = SrcB; result[31:0] = ALUResult
endmodule

// CU
module Control_Unit (
  input  [5:0] HIGH6,
  input  [5:0] LOW6,
  output MemtoReg,
  output MemWrite,
  output Branch,
  output [2:0] ALUControl,
  output ALUSrc,
  output RegDst,
  output Byte_Op,
  output jump,
  output jr,
  output RegWrite
);

  wire add_signal, addu_c, beq_c, lb_c, lui_c, lui_signal, lw_c, nop_c, op0_not, op1_not, op2_not, op3_not,
       op4_not, op5_not, or_signal, ori_c, sb_c, sub_signal, subu_c, sw_c, tag0_not, tag1_not, tag2_not,
       tag3_not, tag4_not, tag5_not;

  and addu (addu_c, tag0_not, tag1_not, tag2_not, tag3_not, tag4_not, tag5_not, LOW6[0], op1_not, op2_not, op3_not, op4_not, LOW6[5]);
  and subu (subu_c, tag0_not, tag1_not, tag2_not, tag3_not, tag4_not, tag5_not, LOW6[0], LOW6[1], op2_not, op3_not, op4_not, LOW6[5]);
  and NOP (nop_c, tag0_not, tag1_not, tag2_not, tag3_not, tag4_not, tag5_not, op0_not, op1_not, op2_not, op3_not, op4_not, op5_not);
  and u_JR (jr, tag0_not, tag1_not, tag2_not, tag3_not, tag4_not, tag5_not, op0_not, op1_not, op2_not, LOW6[3], op4_not, op5_not);
  not not_1 (tag0_not, HIGH6[0]);
  not not_2 (tag1_not, HIGH6[1]);
  not not_3 (tag3_not, HIGH6[3]);
  not not_4 (tag5_not, HIGH6[5]);
  not not_5 (op1_not, LOW6[1]);
  not not_6 (op3_not, LOW6[3]);
  not not_7 (op5_not, LOW6[5]);
  not not_8 (tag2_not, HIGH6[2]);
  not not_9 (tag4_not, HIGH6[4]);
  not not_10 (op0_not, LOW6[0]);
  not not_11 (op2_not, LOW6[2]);
  not not_12 (op4_not, LOW6[4]);
  and SW (sw_c, HIGH6[0], HIGH6[1], tag2_not, HIGH6[3], tag4_not, HIGH6[5]);
  and BEQ (beq_c, tag0_not, tag1_not, HIGH6[2], tag3_not, tag4_not, tag5_not);
  and LUI (lui_c, HIGH6[0], HIGH6[1], HIGH6[2], HIGH6[3], tag4_not, tag5_not);
  and LW (lw_c, HIGH6[0], HIGH6[1], tag2_not, tag3_not, tag4_not, HIGH6[5]);
  and ORI (ori_c, HIGH6[0], tag1_not, HIGH6[2], HIGH6[3], tag4_not, tag5_not);
  and J (jump, tag0_not, HIGH6[1], tag2_not, tag3_not, tag4_not, tag5_not);
  and LB (lb_c, tag0_not, tag1_not, tag2_not, tag3_not, tag4_not, HIGH6[5]);
  and SB (sb_c, tag0_not, tag1_not, tag2_not, HIGH6[3], tag4_not, HIGH6[5]);
  or or_1 (add_signal, addu_c, sw_c, lw_c, lb_c, sb_c);
  or or_2 (sub_signal, subu_c, beq_c, nop_c, jump);
  buf or_3 (or_signal, ori_c);  // OR_Gate
  buf or_4 (lui_signal, lui_c);  // OR_Gate
  or or_5 (Byte_Op, lb_c, sb_c);
  or or_6 (MemtoReg, lw_c, lb_c);
  or or_7 (MemWrite, sw_c, sb_c);
  buf or_8 (Branch, beq_c);  // OR_Gate
  Priority_Encoder priority_encoder_1 (
    .in0(add_signal), .in1(sub_signal), .in2(or_signal), .in3(lui_signal), .out(ALUControl));  // open: in4, in5, in6, in7, en_in, gs, en_out
  or or_9 (ALUSrc, lw_c, sw_c, lui_c, ori_c, lb_c, sb_c);
  or or_10 (RegDst, addu_c, subu_c);
  or or_11 (RegWrite, addu_c, subu_c, lw_c, lui_c, ori_c, lb_c);

  // Other names for the same wires on the sheet: tag0 = HIGH6[0]; tag1 = HIGH6[1]; tag2 = HIGH6[2]; tag3 = HIGH6[3];
  //   tag4 = HIGH6[4]; tag5 = HIGH6[5]; J = jump; op0 = LOW6[0]; op1 = LOW6[1]; op2 = LOW6[2]; op3 = LOW6[3];
  //   op4 = LOW6[4]; op5 = LOW6[5]
endmodule

// OR
module _32bit_or (
  input  [31:0] in_1,
  input  [31:0] in_2,
  output [31:0] out_3
);

  wire [31:0] shifter_1_out, shifter_2_out;

  Shifter #(.width(32)) shifter_1 (.in(in_2), .\dist (5'b10000), .out(shifter_1_out));
  Shifter #(.width(32), .shift("lr")) shifter_2 (.in(shifter_1_out), .\dist (5'b10000), .out(shifter_2_out));
  assign out_3 = in_1 | shifter_2_out;  // OR_Gate or_1, 32 bits wide
endmodule

module NPC (
  input  [31:0] in_1,
  input  [31:0] in_2,
  input  [31:0] in_3,
  input  [31:0] in_4,
  input  in_5,
  input  in_6,
  input  in_7,
  input  in_8,
  output [31:0] NPC
);

  wire PCSrc;
  wire [1:0] or_2_out;
  wire [31:0] J, Jr, PCPlus4;

  Adder #(.width(32)) adder_1 (.a(32'h4), .b(in_1), .out(PCPlus4));  // open: cin, cout
  Multiplexer #(.select(2), .width(32)) multiplexer_1 (
    .in0(PCPlus4), .in1(in_3), .in2(J), .in3(Jr), .out(NPC), .sel(or_2_out));  // open: en
  or or_1 (or_2_out[1], in_5, in_6);
  or or_2 (or_2_out[0], in_6, PCSrc);
  Subtractor #(.width(32)) subtractor_1 (.a(in_4), .b(32'h3000), .out(Jr));  // open: bin, bout
  and and_1 (PCSrc, in_7, in_8);
  Subtractor #(.width(32)) subtractor_2 (
    .a({in_1[31:28], in_2[25:0], 2'b00}), .b(32'h3000), .out(J));  // open: bin, bout

  // Other names for the same wires on the sheet: Instr[31:0] = in_2; PC_value[31:0] = in_1; Branch = in_7;
  //   J_Control = in_5; Jr_Control = in_6; PCBranch[31:0] = in_3; Register_Read_A[31:0] = in_4; ZeroSignal = in_8
endmodule
